// Logisim project s-mips.circ as structural Verilog
module S_MIPS_Board (
  input  DESHABILITAR_DISPATCHER,
  output halt
);

  wire button_1_out, CLK, CS, d_ff_1_q, LCLR, LoadRAM, LoadRAMOn, LW, R_R_W, R_W, ram_dispatcher_1_finished,
       RCS, Reset_out, RST, TTY_EN;
  wire [2:0] KDB;
  wire [3:0] LMask, Mask, ram_1_read_time, ram_1_write_time, RMask;
  wire [6:0] KDB_DATA, TTY_DATA;
  wire [15:0] Addr, LAddr, RAddr;
  wire [31:0] I0, I1, I2, I3, LData, ram_1_data_out_0, ram_1_data_out_1, ram_1_data_out_2, ram_1_data_out_3,
       RI0, RI1, RI2, RI3;

  TTY #(.rows(25), .cols(80)) tty_1 (.data(TTY_DATA), .clk(CLK), .we(TTY_EN), .clr(RST));
  not not_1 (LoadRAMOn, ram_dispatcher_1_finished);
  RAM_Dispatcher ram_dispatcher_1 (
    .WriteTime(ram_1_write_time), .Clock(CLK), .Data(LData), .Address(LAddr), .Mask(LMask),
    .Finished(ram_dispatcher_1_finished), .Write(LW), .CLR(LCLR));
  Keyboard #(.buflen(64)) keyboard_1 (.clk(CLK), .re(KDB[0]), .avail(KDB[2]), .data(KDB_DATA));  // open: clr
  RAM ram_1 (
    .Address(RAddr), .Data_Out_0(ram_1_data_out_0), .Data_Out_1(ram_1_data_out_1),
    .Data_Out_2(ram_1_data_out_2), .Data_Out_3(ram_1_data_out_3), .Data_In_0(RI0), .Data_In_1(RI1),
    .Data_In_2(RI2), .Data_In_3(RI3), .Mask(RMask), .nRead_Write(R_R_W), .Chip_Select(RCS),
    .Read_Time(ram_1_read_time), .Reset(button_1_out), .Write_Time(ram_1_write_time));
  Button button_1 (.out(button_1_out));
  D_Flip_Flop d_ff_1 (.clk(CLK), .D(1'b1), .Q(d_ff_1_q), .reset(Reset_out));  // open: Qn, preset, en
  Button Reset (.out(Reset_out));
  S_MIPS s_mips_1 (
    .Kbd_Enable(KDB[0]), .Address(Addr), .Kbd_Clear(KDB[1]), .Kbd_Available(KDB[2]), .RAM_In_0(I0),
    .Kbd_ASCII_Data(KDB_DATA), .RAM_In_1(I1), .TTY_Enable(TTY_EN), .RAM_In_2(I2), .RAM_In_3(I3),
    .TTY_ASCII_Data(TTY_DATA), .Reset(RST), .RAM_Out_0(ram_1_data_out_0), .Clock(CLK),
    .RAM_Out_1(ram_1_data_out_1), .Stop(halt), .RAM_Out_2(ram_1_data_out_2), .RAM_Out_3(ram_1_data_out_3),
    .Mask(Mask), .Read_Time(ram_1_read_time), .Write_Time(ram_1_write_time), .nRead_Write(R_W),
    .Chip_Select(CS));
  D_Flip_Flop d_ff_2 (.clk(CLK), .D(d_ff_1_q), .Qn(LCLR), .reset(Reset_out));  // open: Q, preset, en
  or or_1 (RST, LCLR, LoadRAM);
  Clock clock_1 (.out(CLK));
  Multiplexer #(.width(32), .enable("false")) multiplexer_1 (.in0(I0), .in1(LData), .out(RI0), .sel(LoadRAM));
  Multiplexer #(.width(32), .enable("false")) multiplexer_2 (.in0(I1), .in1(LData), .out(RI1), .sel(LoadRAM));
  Multiplexer #(.width(32), .enable("false")) multiplexer_3 (.in0(I2), .in1(LData), .out(RI2), .sel(LoadRAM));
  Multiplexer #(.width(32), .enable("false")) multiplexer_4 (.in0(I3), .in1(LData), .out(RI3), .sel(LoadRAM));
  and and_1 (LoadRAM, ~DESHABILITAR_DISPATCHER, LoadRAMOn);  // AND_Gate
  Multiplexer #(.width(16), .enable("false")) multiplexer_5 (.in0(Addr), .in1(LAddr), .out(RAddr), .sel(LoadRAM));
  Multiplexer #(.width(4), .enable("false")) multiplexer_6 (.in0(Mask), .in1(LMask), .out(RMask), .sel(LoadRAM));
  Multiplexer #(.enable("false")) multiplexer_7 (.in0(CS), .in1(LW), .out(RCS), .sel(LoadRAM));
  Multiplexer #(.enable("false")) multiplexer_8 (.in0(R_W), .in1(LW), .out(R_R_W), .sel(LoadRAM));

  // Notes on the sheet:
  //   NO MODIFICAR
  //   Keyboard
endmodule

module RAM (
  input  [15:0] Address,
  input  [31:0] Data_In_0,
  input  [31:0] Data_In_1,
  input  [31:0] Data_In_2,
  input  [31:0] Data_In_3,
  input  [3:0] Mask,
  input  nRead_Write,
  input  Chip_Select,
  input  Reset,
  output [31:0] Data_Out_0,
  output [31:0] Data_Out_1,
  output [31:0] Data_Out_2,
  output [31:0] Data_Out_3,
  output [3:0] Read_Time,
  output [3:0] Write_Time
);

  wire and_2_out, and_3_out, and_4_out, and_5_out, and_6_out, and_7_out, and_8_out, and_9_out, Changed, CLK,
       comparator_2_eq, comparator_3_eq, comparator_4_eq, comparator_5_eq, comparator_6_eq, Count,
       demultiplexer_3_out0, Idle, Idle_q, Load, Load0, Load1, nand_1_out, or_1_out, or_2_out, or_3_out,
       or_4_out, or_5_out, or_6_out, or_7_out, or_8_out, or_9_out, or_10_out, Proc_q, Update_Mem, Zero_Time;
  wire [3:0] counter_1_q, multiplexer_1_out, subtractor_1_out;
  wire [31:0] register_1_q, register_2_q, register_3_q, register_4_q, register_5_q;

  // Probe on 4'b0011
  // Probe on 4'b0010
  Multiplexer #(.width(4), .enable("false")) multiplexer_1 (
    .in0(4'b0011), .in1(4'b0010), .out(multiplexer_1_out), .sel(nRead_Write));
  or or_1 (or_1_out, Idle, Update_Mem);
  or or_2 (or_2_out, ~Chip_Select, Reset);  // OR_Gate
  Subtractor #(.width(4)) subtractor_1 (.a(multiplexer_1_out), .b(4'b0010), .out(subtractor_1_out));  // open: bin, bout
  Demultiplexer #(.enable("false")) demultiplexer_1 (.out0(Idle), .out1(Load0), .in(Idle_q), .sel(Changed));
  D_Flip_Flop u_Idle (.clk(CLK), .D(or_1_out), .Q(Idle_q), .preset(or_2_out));  // open: Qn, en, reset
  // Probe on counter_1_q
  Counter #(.width(4), .max('hf)) counter_1 (
    .load(Load), .D(subtractor_1_out), .count(Count), .Q(counter_1_q), .clk(CLK), .clr(or_3_out));  // open: carry
  or or_3 (or_3_out, ~Chip_Select, Reset);  // OR_Gate
  Comparator #(.width(4), .mode("unsigned")) comparator_1 (
    .a(4'b0000), .b(counter_1_q), .eq(Zero_Time));  // open: gt, lt
  or or_4 (or_4_out, Count, Load0, Load1);
  Register #(.width(32)) register_1 (.D(Data_In_0), .en(Chip_Select), .Q(register_1_q), .clk(CLK), .clr(or_5_out));
  or or_5 (or_5_out, ~Chip_Select, Reset);  // OR_Gate
  Register #(.width(32)) register_2 (.D(Data_In_1), .en(Chip_Select), .Q(register_2_q), .clk(CLK), .clr(or_6_out));
  or or_6 (or_6_out, ~Chip_Select, Reset);  // OR_Gate
  Register #(.width(32)) register_3 (.D(Data_In_2), .en(Chip_Select), .Q(register_3_q), .clk(CLK), .clr(or_7_out));
  or or_7 (or_7_out, ~Chip_Select, Reset);  // OR_Gate
  Register #(.width(32)) register_4 (.D(Data_In_3), .en(Chip_Select), .Q(register_4_q), .clk(CLK), .clr(or_8_out));
  or or_8 (or_8_out, ~Chip_Select, Reset);  // OR_Gate
  Register #(.width(32)) register_5 (
    .D({{11{1'b1}}, nRead_Write, Mask, Address}), .en(Chip_Select), .Q(register_5_q), .clk(CLK),
    .clr(or_9_out));
  or or_9 (or_9_out, ~Chip_Select, Reset);  // OR_Gate
  D_Flip_Flop Proc (.clk(CLK), .D(or_4_out), .Q(Proc_q), .reset(or_10_out));  // open: Qn, preset, en
  or or_10 (or_10_out, ~Chip_Select, Reset);  // OR_Gate
  Demultiplexer #(.enable("false")) demultiplexer_2 (
    .out0(Count), .out1(Update_Mem), .in(demultiplexer_3_out0), .sel(Zero_Time));
  Demultiplexer #(.enable("false")) demultiplexer_3 (
    .out0(demultiplexer_3_out0), .out1(Load1), .in(Proc_q), .sel(Changed));
  Clock clock_1 (.out(CLK));
  Comparator #(.width(32)) comparator_2 (.a(register_1_q), .b(Data_In_0), .eq(comparator_2_eq));  // open: gt, lt
  Comparator #(.width(32)) comparator_3 (.a(register_2_q), .b(Data_In_1), .eq(comparator_3_eq));  // open: gt, lt
  Comparator #(.width(32)) comparator_4 (.a(register_3_q), .b(Data_In_2), .eq(comparator_4_eq));  // open: gt, lt
  Comparator #(.width(32)) comparator_5 (.a(register_4_q), .b(Data_In_3), .eq(comparator_5_eq));  // open: gt, lt
  Comparator #(.width(32)) comparator_6 (
    .a(register_5_q), .b({{11{1'b1}}, nRead_Write, Mask, Address}), .eq(comparator_6_eq));  // open: gt, lt
  nand nand_1 (nand_1_out, comparator_6_eq, comparator_2_eq, comparator_3_eq, comparator_4_eq, comparator_5_eq);
  and and_1 (Changed, nand_1_out, Chip_Select);
  or or_11 (Load, Count, Load1, Load0);
  and and_2 (and_2_out, Mask[0], Update_Mem, nRead_Write);
  and and_3 (and_3_out, Mask[1], Update_Mem, nRead_Write);
  and and_4 (and_4_out, Mask[2], Update_Mem, nRead_Write);
  and and_5 (and_5_out, Mask[3], Update_Mem, nRead_Write);
  RAM_part #(.addrWidth(16), .dataWidth(32), .bus("separate")) ram_1 (
    .addr(Address), .din(Data_In_0), .data(Data_Out_0), .str(and_2_out), .sel(Chip_Select), .clk(CLK),
    .ld(and_6_out), .clr(Reset));
  and and_6 (and_6_out, ~nRead_Write, Idle);  // AND_Gate
  RAM_part #(.addrWidth(16), .dataWidth(32), .bus("separate")) ram_2 (
    .addr(Address), .din(Data_In_1), .data(Data_Out_1), .str(and_3_out), .sel(Chip_Select), .clk(CLK),
    .ld(and_7_out), .clr(Reset));
  and and_7 (and_7_out, ~nRead_Write, Idle);  // AND_Gate
  RAM_part #(.addrWidth(16), .dataWidth(32), .bus("separate")) ram_3 (
    .addr(Address), .din(Data_In_2), .data(Data_Out_2), .str(and_4_out), .sel(Chip_Select), .clk(CLK),
    .ld(and_8_out), .clr(Reset));
  and and_8 (and_8_out, ~nRead_Write, Idle);  // AND_Gate
  RAM_part #(.addrWidth(16), .dataWidth(32), .bus("separate")) ram_4 (
    .addr(Address), .din(Data_In_3), .data(Data_Out_3), .str(and_5_out), .sel(Chip_Select), .clk(CLK),
    .ld(and_9_out), .clr(Reset));
  and and_9 (and_9_out, ~nRead_Write, Idle);  // AND_Gate

  assign Read_Time = 4'b0011;
  assign Write_Time = 4'b0010;

  // Other names for the same wires on the sheet: M0 = Mask[0]; M1 = Mask[1]; M2 = Mask[2]; M3 = Mask[3];
  //   RW = nRead_Write; CLR = Reset; CS = Chip_Select; Load2 = Count

  // Notes on the sheet:
  //   NO MODIFICAR
  //   excepto quizás los valores RT y WT
  //   BANK0
  //   BANK1
  //   BANK2
  //   BANK3
endmodule

module S_MIPS (
  input  Kbd_Available,
  input  [6:0] Kbd_ASCII_Data,
  input  [31:0] RAM_Out_0,
  input  [31:0] RAM_Out_1,
  input  Reset,
  input  [31:0] RAM_Out_2,
  input  Clock,
  input  [31:0] RAM_Out_3,
  input  [3:0] Read_Time,
  input  [3:0] Write_Time,
  output Kbd_Enable,
  output [15:0] Address,
  output Kbd_Clear,
  output TTY_Enable,
  output [6:0] TTY_ASCII_Data,
  output Stop,
  output [31:0] RAM_In_0,
  output [31:0] RAM_In_1,
  output [31:0] RAM_In_2,
  output [31:0] RAM_In_3,
  output [3:0] Mask,
  output nRead_Write,
  output Chip_Select
);

  wire e_SP, en_pc, en_ram_ins, en_ram_p_lw, lw, push, RF_WR, RW;
  wire [1:0] mask2b, mask2b_ram, multiplexer_4_out;
  wire [2:0] op_cu, sel_E;
  wire [3:0] mask_t, RAM_MASK;
  wire [15:0] dir, RAM_A;
  wire [31:0] ER_P_LW, IM, RAM_INPUT, RAM_INPUT_0, RAM_INPUT_1, RAM_INPUT_2, RAM_INPUT_3, RAM_OUTPUT,
       RAM_OUTPUT_0, RAM_OUTPUT_1, RAM_OUTPUT_2, RAM_OUTPUT_3;

  Multiplexer #(.width(16)) multiplexer_1 (.in0(RAM_A), .in1(dir), .out(Address), .sel(en_ram_ins));  // open: en
  inv inv_1 (.in_1(RAM_Out_0), .out_2(RAM_OUTPUT_0));
  inv inv_2 (.in_1(RAM_Out_1), .out_2(RAM_OUTPUT_1));
  inv inv_3 (.in_1(RAM_Out_2), .out_2(RAM_OUTPUT_2));
  inv inv_4 (.in_1(RAM_Out_3), .out_2(RAM_OUTPUT_3));
  inv inv_5 (.in_1(RAM_INPUT_0), .out_2(RAM_In_0));
  inv inv_6 (.in_1(RAM_INPUT_1), .out_2(RAM_In_1));
  inv inv_7 (.in_1(RAM_INPUT_2), .out_2(RAM_In_2));
  inv inv_8 (.in_1(RAM_INPUT_3), .out_2(RAM_In_3));
  Multiplexer #(.width(4)) multiplexer_2 (.in0(RAM_MASK), .in1(mask_t), .out(Mask), .sel(en_ram_ins));  // open: en
  not not_1 (nRead_Write, RW);
  // Probe on mask2b
  CU cu_1 (
    .in_2(op_cu), .in_5(sel_E), .in_4(Read_Time), .in_6(Write_Time), .in_7(lw), .in_8(push), .RF_WR(RF_WR),
    .tty(TTY_Enable), .kbd(Kbd_Enable), .halt(Stop), .enable_PC(en_pc), .CS(Chip_Select), .in_1(Reset),
    .in_3(Clock), .leer_ram(RW), .en_ram_ins(en_ram_ins), .en_ram_p_lw(en_ram_p_lw), .e_SP(e_SP));
  Data_Path data_path_1 (
    .Enable_PC(en_pc), .in_4(RF_WR), .in_5(Reset), .in_6(Clock), .in_8(ER_P_LW), .Dir_RAM(RAM_A),
    .Mask_RAM(RAM_MASK), .Mask2b_RAM(mask2b_ram), .out_15(RAM_INPUT), .in_1(IM), .Dir(dir), .Mask(mask_t),
    .Mask2b(mask2b), .kbd(Kbd_ASCII_Data), .tty_data(TTY_ASCII_Data), .op_cu(op_cu), .push(push), .lw(lw),
    .Sesp(sel_E), .Enable_SP(e_SP));  // open: tty, kbd_2
  Multiplexer #(.select(2), .width(32)) multiplexer_3 (
    .in0(RAM_OUTPUT_0), .in1(RAM_OUTPUT_1), .in2(RAM_OUTPUT_2), .in3(RAM_OUTPUT_3), .out(RAM_OUTPUT),
    .sel(multiplexer_4_out));  // open: en
  Multiplexer #(.width(2)) multiplexer_4 (
    .in0(mask2b_ram), .in1(mask2b), .out(multiplexer_4_out), .sel(en_ram_ins));  // open: en
  // Probe on RAM_OUTPUT
  Register #(.width(32)) register_1 (.D(RAM_OUTPUT), .en(en_ram_ins), .Q(IM), .clk(Clock), .clr(Reset));
  // Probe on IM
  Register #(.width(32)) register_2 (.D(RAM_OUTPUT), .en(en_ram_p_lw), .Q(ER_P_LW), .clk(Clock), .clr(Reset));
  // Probe on ER_P_LW
  // Probe on RAM_INPUT
  Demultiplexer #(.select(2), .width(32)) demultiplexer_1 (
    .out0(RAM_INPUT_0), .out1(RAM_INPUT_1), .out2(RAM_INPUT_2), .out3(RAM_INPUT_3), .in(RAM_INPUT),
    .sel(mask2b_ram));  // open: en

  // Other names for the same wires on the sheet: CLK = Clock; CLR = Reset; CS = Chip_Select;
  //   KBD_AVAIL = Kbd_Available; KBD_CLR = Kbd_Clear; KBD_DATA[6:0] = Kbd_ASCII_Data; TTY_DATA[6:0] = TTY_ASCII_Data

  // Notes on the sheet:
  //   RAM ADDRESS
  //   DATA FROM RAM
  //   DATA TO RAM
  //   DATA WRITE MASK
  //   RAM TIMING
  //   RAM CONTROL
  //   KEYBOARD
  //   TTY
  //   SEQUENCING
endmodule

module RAM_Dispatcher (
  input  [3:0] WriteTime,
  input  Clock,
  input  CLR,
  output [31:0] Data,
  output [15:0] Address,
  output [3:0] Mask,
  output Finished,
  output Write
);

  wire demultiplexer_2_out1, demultiplexer_3_out1, End, IDLE_q, IncAddr, Load, or_1_out, or_2_out, While_q,
       WriteEnd;
  wire [3:0] counter_1_q;
  wire [31:0] CurrentAddress_q;

  Counter #(.width(32), .max('hffffffff)) CurrentAddress (
    .count(IncAddr), .Q({CurrentAddress_q[31:18], Address, CurrentAddress_q[1:0]}), .clk(Clock), .clr(CLR));  // open: load, D, carry
  or or_1 (or_1_out, IncAddr, demultiplexer_3_out1, Finished);
  D_Flip_Flop IDLE (.clk(Clock), .D(or_1_out), .Q(IDLE_q), .preset(CLR));  // open: Qn, en, reset
  Demultiplexer #(.enable("false")) demultiplexer_1 (.out0(Load), .out1(Finished), .in(IDLE_q), .sel(End));
  D_Flip_Flop While (.clk(Clock), .D(or_2_out), .Q(While_q), .reset(CLR));  // open: Qn, preset, en
  or or_2 (or_2_out, Write, Load);
  RAM_part #(.addrWidth(18), .dataWidth(32)) ram_1 (
    .addr({Address, CurrentAddress_q[1:0]}), .data(Data), .clk(Clock));  // open: sel, ld, clr
  Demultiplexer #(.enable("false")) demultiplexer_2 (
    .out0(Write), .out1(demultiplexer_2_out1), .in(While_q), .sel(WriteEnd));
  Decoder #(.select(2)) decoder_1 (
    .out0(Mask[0]), .out1(Mask[1]), .out2(Mask[2]), .out3(Mask[3]), .sel(CurrentAddress_q[1:0]));  // open: en
  Demultiplexer #(.enable("false")) demultiplexer_3 (
    .out0(IncAddr), .out1(demultiplexer_3_out1), .in(demultiplexer_2_out1), .sel(End));
  Counter #(.width(4), .max('hf)) counter_1 (
    .load(Load), .D(WriteTime), .count(Write), .Q(counter_1_q), .clk(Clock));  // open: carry, clr
  Comparator #(.width(32)) comparator_1 (.a(Data), .b({32{1'b1}}), .eq(End));  // open: gt, lt
  Comparator #(.width(4)) comparator_2 (.a(4'b0000), .b(counter_1_q), .eq(WriteEnd));  // open: gt, lt

  // Other names for the same wires on the sheet: CLK = Clock; Count = Write; WT[3:0] = WriteTime
endmodule

module ALU (
  input  [31:0] in_1,
  input  [31:0] in_2,
  input  [15:0] in_3,
  input  [4:0] in_4,
  input  enable,
  output [31:0] Output,
  output [31:0] hi
);

  wire [31:0] hiDiv, hiDivu, hiMul, hiMulu, ResultAddi, ResultAnd, ResultAndi, ResultDiv, ResultDivu,
       ResultMul, ResultMulu, ResultNor, ResultOr, ResultOri, ResultSlt, ResultSlti, ResultSltiu, ResultSltu,
       ResultSub, ResultSum, ResultXor, ResultXori;

  // Probe on ResultAddi
  Adder #(.width(32)) adder_1 (.a(in_1), .b(in_2), .out(ResultSum));  // open: cin, cout
  assign ResultAnd = in_1 & in_2;  // AND_Gate and_1, 32 bits wide
  addi addi_1 (.in_1(in_1), .in_2(in_3), .out(ResultAddi));
  andi_ori_xori andi_ori_xori_1 (.in_2(in_1), .in_3(in_3), .out(ResultOri), .in_1(2'b01));
  div_divu div_divu_1 (.in_1(in_1), .in_3(in_2), .out_lo(ResultDiv), .out_hi(hiDiv), .in_2(1'b0));
  // Probe on in_4
  Subtractor #(.width(32)) subtractor_1 (.a(in_1), .b(in_2), .out(ResultSub));  // open: bin, bout
  // Probe on ResultDivu
  div_divu div_divu_2 (.in_1(in_1), .in_3(in_2), .out_lo(ResultDivu), .out_hi(hiDivu), .in_2(1'b1));
  // Probe on hiDivu
  assign ResultOr = in_1 | in_2;  // OR_Gate or_1, 32 bits wide
  slti_sltiu slti_sltiu_1 (.in_1(in_1), .in_3(in_3), .out(ResultSlti), .in_2(1'b0));
  andi_ori_xori andi_ori_xori_2 (.in_2(in_1), .in_3(in_3), .out(ResultXori), .in_1(2'b10));
  Multiplexer #(.select(5), .width(32)) multiplexer_1 (
    .in1(ResultSum), .in2(ResultSub), .in3(ResultMul), .in4(ResultMulu), .in5(ResultDiv), .in6(ResultDivu),
    .in7(ResultSlt), .in8(ResultSltu), .in9(ResultAnd), .in10(ResultOr), .in11(ResultNor), .in12(ResultXor),
    .in13(ResultAddi), .in14(ResultSlti), .in15(ResultSltiu), .in16(ResultAndi), .in17(ResultOri),
    .in18(ResultXori), .out(Output), .sel(in_4), .en(enable));  // open: in0, in19, in20, in21, in22, in23, in24, in25, in26, in27, in28, in29, in30, in31
  // Probe on Output
  mul_mulu mul_mulu_1 (.in_1(in_1), .in_3(in_2), .out_lo(ResultMul), .out_hi(hiMul), .in_2(1'b0));
  slt_sltu slt_sltu_1 (.in_1(in_1), .in_3(in_2), .out(ResultSlt), .in_2(1'b0));
  assign ResultNor = ~(in_1 | in_2);  // NOR_Gate nor_1, 32 bits wide
  slti_sltiu slti_sltiu_2 (.in_1(in_1), .in_3(in_3), .out(ResultSltiu), .in_2(1'b1));
  mul_mulu mul_mulu_2 (.in_1(in_1), .in_3(in_2), .out_lo(ResultMulu), .out_hi(hiMulu), .in_2(1'b1));
  slt_sltu slt_sltu_2 (.in_1(in_1), .in_3(in_2), .out(ResultSltu), .in_2(1'b1));
  assign ResultXor = in_1 ^ in_2;  // XOR_Gate xor_1, 32 bits wide
  andi_ori_xori andi_ori_xori_3 (.in_2(in_1), .in_3(in_3), .out(ResultAndi), .in_1(2'b00));
  // Probe on in_4[1:0]
  Multiplexer #(.select(2), .width(32)) multiplexer_2 (
    .in0(hiDiv), .in1(hiDivu), .in2(hiMul), .in3(hiMulu), .out(hi), .sel(in_4[1:0]));  // open: en
  // Probe on Output

  // Other names for the same wires on the sheet: a[31:0] = in_1; b[31:0] = in_2; constante[15:0] = in_3; e = enable;
  //   Result[31:0] = Output; selector[4:0] = in_4; selector_u[1:0] = in_4[1:0]
endmodule

module Prueba (
  input  mul_div,
  input  [4:0] Rt,
  input  en_pila,
  input  [4:0] Rs,
  input  bRam,
  input  [4:0] Rd,
  input  alu,
  input  [4:0] Salu,
  input  [15:0] cte,
  input  Sbc,
  input  [2:0] bc,
  input  jr,
  input  [25:0] cte_2,
  input  [2:0] Sesp,
  input  [1:0] sel_HL,
  input  tipo_i,
  input  j,
  input  [2:0] op_CU,
  input  bPila,
  input  rnd,
  output mul_div_2,
  output CS,
  output bRam_2,
  output alu_2,
  output [4:0] Salu_2,
  output Sbc_2,
  output [2:0] bc_2,
  output jr_2,
  output [2:0] Sesp_2,
  output [1:0] sel_HL_2,
  output tipo_i_2,
  output j_2,
  output [2:0] op_CU_2,
  output bPila_2,
  output rnd_2,
  output [4:0] Rt_2,
  output [4:0] Rs_2,
  output [4:0] Rd_2,
  output [15:0] cte_3,
  output [25:0] cte_4
);

  wire ALU_I1, clk, comparator_1_eq, comparator_2_gt, d_ff_1_q, demultiplexer_1_out0, demultiplexer_2_out5,
       en_adr, en_count, Enable_Pc0, halt1, jump_nada, kbd1, not_1_out, not_2_out, or_1_out, pila1, ram1,
       reset, rnd1, rset, tty1;
  wire [1:0] sel_out_ram;
  wire [2:0] Operador_E, tipo_operacion;
  wire [15:0] adder_3_out, cont_adr;
  wire [31:0] adder_1_out, adder_2_out, cont, divider_2_rem, random_1_out;
  wire [31:2] sel_out_ram0;

  not not_1 (not_1_out, reset);
  D_Flip_Flop #(.trigger("falling")) d_ff_1 (
    .clk(clk), .D(or_1_out), .Q(d_ff_1_q), .reset(reset));  // open: Qn, preset, en
  Demultiplexer demultiplexer_1 (
    .out0(demultiplexer_1_out0), .out1(Enable_Pc0), .in(d_ff_1_q), .sel(not_2_out));  // open: en
  or or_1 (or_1_out, demultiplexer_1_out0, not_1_out);
  not not_2 (not_2_out, reset);
  Demultiplexer #(.select(3)) demultiplexer_2 (
    .out1(ALU_I1), .out2(jump_nada), .out3(ram1), .out4(pila1), .out5(demultiplexer_2_out5), .in(Enable_Pc0),
    .sel(tipo_operacion));  // open: out0, out6, out7, en
  Adder #(.width(32)) adder_1 (.a(cont), .b(32'h1), .out(adder_1_out));  // open: cin, cout
  Demultiplexer #(.select(3)) demultiplexer_3 (
    .out1(halt1), .out2(tty1), .out3(rnd1), .out4(kbd1), .in(demultiplexer_2_out5), .sel(Operador_E));  // open: out0, out5, out6, out7, en
  Register #(.width(32)) register_1 (.D(adder_1_out), .Q(cont));  // open: en, clk, clr
  Register #(.width(32)) register_2 ();  // open: D, en, Q, clk, clr
  Divider #(.width(32)) divider_1 (.a(cont), .b(32'h4), .rem({sel_out_ram0, sel_out_ram}));  // open: out, upper
  Adder #(.width(32)) adder_2 (.a(cont), .b(32'h1), .out(adder_2_out));  // open: cin, cout
  Divider #(.width(32)) divider_2 (.a(cont), .b(32'h10), .rem(divider_2_rem));  // open: out, upper
  Comparator #(.width(32)) comparator_1 (.b({32{1'b0}}), .eq(comparator_1_eq));  // open: a, gt, lt
  Register #(.width(32)) register_3 (.D(adder_2_out), .en(en_count), .Q(cont));  // open: clk, clr
  Comparator #(.width(32)) comparator_2 (.a(cont), .b({32{1'b0}}), .gt(comparator_2_gt));  // open: eq, lt
  Random #(.width(32)) random_1 (.clk(clk), .next(rnd), .out(random_1_out), .clr(rset));
  // Probe on random_1_out
  or or_2 (en_adr, comparator_1_eq, comparator_2_gt);
  Adder #(.width(16)) adder_3 (.a(cont_adr), .b(16'h1), .out(adder_3_out));  // open: cin, cout
  Register #(.width(16)) register_4 (.D(adder_3_out), .en(en_adr), .Q(cont_adr));  // open: clk, clr

  assign alu_2 = alu;
  assign bc_2 = bc;
  assign bPila_2 = bPila;
  assign bRam_2 = bRam;
  assign CS = en_pila;
  assign cte_3 = cte;
  assign cte_4 = cte_2;
  assign j_2 = j;
  assign jr_2 = jr;
  assign mul_div_2 = mul_div;
  assign op_CU_2 = op_CU;
  assign Rd_2 = Rd;
  assign rnd_2 = rnd;
  assign Rs_2 = Rs;
  assign Rt_2 = Rt;
  assign Salu_2 = Salu;
  assign Sbc_2 = Sbc;
  assign sel_HL_2 = sel_HL;
  assign Sesp_2 = Sesp;
  assign tipo_i_2 = tipo_i;

  // Other names for the same wires on the sheet: destino[25:0] = cte_2; sel_out_ram0[1:0] = sel_out_ram

  // Notes on the sheet:
  //   ojo con esto (pie de Leo)
endmodule

module RF (
  input  [31:0] Input,
  input  [31:0] lo,
  input  [31:0] hi,
  input  [1:0] in_4,
  input  RW,
  input  Reset,
  input  clock,
  input  mul_div,
  input  in_9,
  input  in_10,
  input  e_sp,
  input  [4:0] Selector_B,
  input  [4:0] Selector_A,
  input  [4:0] Selector,
  output [31:0] Output_A,
  output [31:0] Output_B,
  output [31:0] Output_hi,
  output [31:0] Output_lo,
  output [31:0] Output_SP
);

  wire and_1_out, e0, e1, e2, e3, e4, e5, e6, e7, e8, e9, e10, e11, e12, e13, e14, e15, e16, e17, e18, e19,
       e20, e21, e22, e23, e24, e25, e26, e27, e28, e29, e30, e31, ehi, elo, multiplexer_3_out;
  wire [31:0] input_t, multiplexer_1_out, multiplexer_2_out, o1, o2, o3, o4, o5, o6, o7, o8, o9, o10, o11,
       o12, o13, o14, o15, o16, o17, o18, o19, o20, o21, o22, o23, o24, o25, o26, o27, o28, o29, o30, Vpop,
       Vpush;

  Register #(.width(32)) r1 (.D(input_t), .en(e1), .Q(o1), .clk(clock), .clr(Reset));
  Register #(.width(32)) r8 (.D(input_t), .en(e8), .Q(o8), .clk(clock), .clr(Reset));
  Register #(.width(32)) r15 (.D(input_t), .en(e15), .Q(o15), .clk(clock), .clr(Reset));
  Register #(.width(32)) r22 (.D(input_t), .en(e22), .Q(o22), .clk(clock), .clr(Reset));
  Register #(.width(32)) r29 (.D(input_t), .en(e29), .Q(o29), .clk(clock), .clr(Reset));
  // Probe on o1
  Multiplexer #(.width(32)) multiplexer_1 (
    .in0(Input), .in1(multiplexer_2_out), .out(multiplexer_1_out), .sel(in_9));  // open: en
  Multiplexer #(.width(32)) multiplexer_2 (.in0(Vpop), .in1(Vpush), .out(multiplexer_2_out), .sel(in_10));  // open: en
  Multiplexer multiplexer_3 (.in0(e31), .in1(in_9), .out(multiplexer_3_out), .sel(in_9));  // open: en
  // Probe on Input
  // Probe on Output_hi
  Register #(.width(32)) r2 (.D(input_t), .en(e2), .Q(o2), .clk(clock), .clr(Reset));
  Register #(.width(32)) r9 (.D(input_t), .en(e9), .Q(o9), .clk(clock), .clr(Reset));
  // Probe on o9
  Register #(.width(32)) r16 (.D(input_t), .en(e16), .Q(o16), .clk(clock), .clr(Reset));
  Register #(.width(32)) r23 (.D(input_t), .en(e23), .Q(o23), .clk(clock), .clr(Reset));
  Register #(.width(32)) r30 (.D(input_t), .en(e30), .Q(o30), .clk(clock), .clr(Reset));
  // Probe on Output_SP
  and and_1 (and_1_out, multiplexer_3_out, e_sp);
  Register #(.width(32)) r3 (.D(input_t), .en(e3), .Q(o3), .clk(clock), .clr(Reset));
  // Probe on o3
  Register #(.width(32)) r10 (.D(input_t), .en(e10), .Q(o10), .clk(clock), .clr(Reset));
  // Probe on o10
  Register #(.width(32)) r17 (.D(input_t), .en(e17), .Q(o17), .clk(clock), .clr(Reset));
  Register #(.width(32)) r24 (.D(input_t), .en(e24), .Q(o24), .clk(clock), .clr(Reset));
  Register #(.width(32)) esp (.D(multiplexer_1_out), .en(and_1_out), .Q(Output_SP), .clk(clock), .clr(Reset));
  // Probe on lo
  // Probe on Output_lo
  Register #(.width(32)) r4 (.D(input_t), .en(e4), .Q(o4), .clk(clock), .clr(Reset));
  Register #(.width(32)) r11 (.D(input_t), .en(e11), .Q(o11), .clk(clock), .clr(Reset));
  Register #(.width(32)) r18 (.D(input_t), .en(e18), .Q(o18), .clk(clock), .clr(Reset));
  Register #(.width(32)) r25 (.D(input_t), .en(e25), .Q(o25), .clk(clock), .clr(Reset));
  Comparator #(.width(2), .mode("unsigned")) comparator_1 (.a(in_4), .b(2'b10), .eq(elo));  // open: gt, lt
  // Probe on elo
  Multiplexer #(.select(2), .width(32)) multiplexer_4 (
    .in0(Input), .in1(Output_hi), .in2(Output_lo), .out(input_t), .sel(in_4));  // open: in3, en
  Register #(.width(32)) r5 (.D(input_t), .en(e5), .Q(o5), .clk(clock), .clr(Reset));
  Register #(.width(32)) r12 (.D(input_t), .en(e12), .Q(o12), .clk(clock), .clr(Reset));
  Register #(.width(32)) r19 (.D(input_t), .en(e19), .Q(o19), .clk(clock), .clr(Reset));
  Register #(.width(32)) r26 (.D(input_t), .en(e26), .Q(o26), .clk(clock), .clr(Reset));
  Register #(.width(32)) u_hi (.D(hi), .en(mul_div), .Q(Output_hi), .clk(clock), .clr(Reset));
  // Probe on Output_hi
  Adder #(.width(32)) adder_1 (.a(Output_SP), .b(32'h4), .out(Vpop));  // open: cin, cout
  // Probe on input_t
  Register #(.width(32)) r6 (.D(input_t), .en(e6), .Q(o6), .clk(clock), .clr(Reset));
  Register #(.width(32)) r13 (.D(input_t), .en(e13), .Q(o13), .clk(clock), .clr(Reset));
  Register #(.width(32)) r20 (.D(input_t), .en(e20), .Q(o20), .clk(clock), .clr(Reset));
  Register #(.width(32)) r27 (.D(input_t), .en(e27), .Q(o27), .clk(clock), .clr(Reset));
  // Probe on hi
  Comparator #(.width(2), .mode("unsigned")) comparator_2 (.a(in_4), .b(2'b01), .eq(ehi));  // open: gt, lt
  Subtractor #(.width(32)) subtractor_1 (.a(Output_SP), .b(32'h4), .out(Vpush));  // open: bin, bout
  Register #(.width(32)) r7 (.D(input_t), .en(e7), .Q(o7), .clk(clock), .clr(Reset));
  Register #(.width(32)) r14 (.D(input_t), .en(e14), .Q(o14), .clk(clock), .clr(Reset));
  Register #(.width(32)) r21 (.D(input_t), .en(e21), .Q(o21), .clk(clock), .clr(Reset));
  Register #(.width(32)) r28 (.D(input_t), .en(e28), .Q(o28), .clk(clock), .clr(Reset));
  Register #(.width(32)) u_lo (.D(lo), .en(mul_div), .Q(Output_lo), .clk(clock), .clr(Reset));
  // Probe on Output_lo
  // Probe on o7
  // Probe on e0
  Multiplexer #(.select(5), .width(32), .enable("false")) multiplexer_5 (
    .in0({32{1'b0}}), .in1(o1), .in2(o2), .in3(o3), .in4(o4), .in5(o5), .in6(o6), .in7(o7), .in8(o8),
    .in9(o9), .in10(o10), .in11(o11), .in12(o12), .in13(o13), .in14(o14), .in15(o15), .in16(o16), .in17(o17),
    .in18(o18), .in19(o19), .in20(o20), .in21(o21), .in22(o22), .in23(o23), .in24(o24), .in25(o25),
    .in26(o26), .in27(o27), .in28(o28), .in29(o29), .in30(o30), .in31(Output_SP), .out(Output_A),
    .sel(Selector_A));
  Demultiplexer #(.select(5)) demultiplexer_1 (
    .out0(e0), .out1(e1), .out2(e2), .out3(e3), .out4(e4), .out5(e5), .out6(e6), .out7(e7), .out8(e8),
    .out9(e9), .out10(e10), .out11(e11), .out12(e12), .out13(e13), .out14(e14), .out15(e15), .out16(e16),
    .out17(e17), .out18(e18), .out19(e19), .out20(e20), .out21(e21), .out22(e22), .out23(e23), .out24(e24),
    .out25(e25), .out26(e26), .out27(e27), .out28(e28), .out29(e29), .out30(e30), .out31(e31), .in(RW),
    .sel(Selector));  // open: en
  Multiplexer #(.select(5), .width(32), .enable("false")) multiplexer_6 (
    .in0({32{1'b0}}), .in1(o1), .in2(o2), .in3(o3), .in4(o4), .in5(o5), .in6(o6), .in7(o7), .in8(o8),
    .in9(o9), .in10(o10), .in11(o11), .in12(o12), .in13(o13), .in14(o14), .in15(o15), .in16(o16), .in17(o17),
    .in18(o18), .in19(o19), .in20(o20), .in21(o21), .in22(o22), .in23(o23), .in24(o24), .in25(o25),
    .in26(o26), .in27(o27), .in28(o28), .in29(o29), .in30(o30), .in31(Output_SP), .out(Output_B),
    .sel(Selector_B));

  // Other names for the same wires on the sheet: clk = clock; en_pila = in_9; in_hi[31:0] = hi; in_lo[31:0] = lo;
  //   input0[31:0] = Input; o31[31:0] = Output_SP; push = in_10; rs = Reset; sel_hl[1:0] = in_4
endmodule

module ID (
  input  [31:0] Input,
  output [5:0] Op_Code,
  output [4:0] Rs,
  output [4:0] Rt,
  output [4:0] Rd,
  output [5:0] Func_code,
  output [15:0] constante,
  output [25:0] Destino
);


  assign constante = Input[15:0];
  assign Destino = Input[25:0];
  assign Func_code = Input[5:0];
  assign Op_Code = Input[31:26];
  assign Rd = Input[15:11];
  assign Rs = Input[25:21];
  assign Rt = Input[20:16];

  // Other names for the same wires on the sheet: x[4:0] = Input[10:6]
endmodule

module mul_mulu (
  input  [31:0] in_1,
  input  in_2,
  input  [31:0] in_3,
  output [31:0] out_lo,
  output [31:0] out_hi
);

  wire neg, neg_a, neg_b, xor_1_out;
  wire [31:0] adder_1_out, hi, lo, negator_1_out, negator_2_out, not_1_out, not_2_out, result_a, result_b;

  Negator #(.width(32)) negator_1 (.in(in_1), .out(negator_1_out));
  // Probe on in_1
  // Probe on in_3
  and and_1 (neg_a, in_1[31], ~in_2);  // AND_Gate
  Multiplexer #(.width(32)) multiplexer_1 (.in0(in_1), .in1(negator_1_out), .out(result_a), .sel(neg_a));  // open: en
  and and_2 (neg_b, in_3[31], ~in_2);  // AND_Gate
  Multiplexer #(.width(32)) multiplexer_2 (.in0(in_3), .in1(negator_2_out), .out(result_b), .sel(neg_b));  // open: en
  Negator #(.width(32)) negator_2 (.in(in_3), .out(negator_2_out));
  Multiplier #(.width(32)) multiplier_1 (.a(result_a), .b(result_b), .out(lo), .cout(hi));  // open: cin
  assign not_1_out = ~lo;  // NOT_Gate not_1, 32 bits wide
  xor xor_1 (xor_1_out, in_1[31], in_3[31]);
  Adder #(.width(32)) adder_1 (.a(32'h1), .b(not_1_out), .out(adder_1_out));  // open: cin, cout
  Multiplexer #(.width(32)) multiplexer_3 (.in0(hi), .in1(not_2_out), .out(out_hi), .sel(neg));  // open: en
  assign not_2_out = ~hi;  // NOT_Gate not_2, 32 bits wide
  // Probe on out_lo
  // Probe on out_hi
  and and_3 (neg, xor_1_out, ~in_2);  // AND_Gate
  Multiplexer #(.width(32)) multiplexer_4 (.in0(lo), .in1(adder_1_out), .out(out_lo), .sel(neg));  // open: en

  // Other names for the same wires on the sheet: a[31:0] = in_1; _1er_bit_de_a = in_1[31]; b[31:0] = in_3;
  //   _1er_bit_de_b = in_3[31]; result_hi[31:0] = out_hi; result_lo[31:0] = out_lo; sin_signo = in_2
endmodule

module div_divu (
  input  [31:0] in_1,
  input  in_2,
  input  [31:0] in_3,
  output [31:0] out_lo,
  output [31:0] out_hi
);

  wire neg, neg_a, neg_b, xor_1_out;
  wire [31:0] hi, lo, negator_1_out, negator_2_out, negator_3_out, negator_4_out, result_a, result_b;

  // Probe on in_1
  // Probe on in_3
  Negator #(.width(32)) negator_1 (.in(in_1), .out(negator_1_out));
  and and_1 (neg_a, in_1[31], ~in_2);  // AND_Gate
  Multiplexer #(.width(32)) multiplexer_1 (.in0(in_1), .in1(negator_1_out), .out(result_a), .sel(neg_a));  // open: en
  and and_2 (neg_b, in_3[31], ~in_2);  // AND_Gate
  Multiplexer #(.width(32)) multiplexer_2 (.in0(in_3), .in1(negator_2_out), .out(result_b), .sel(neg_b));  // open: en
  Negator #(.width(32)) negator_2 (.in(in_3), .out(negator_2_out));
  Divider #(.width(32)) divider_1 (.a(result_a), .b(result_b), .out(lo), .rem(hi));  // open: upper
  // Probe on lo
  xor xor_1 (xor_1_out, in_1[31], in_3[31]);
  and and_3 (neg, xor_1_out, ~in_2);  // AND_Gate
  Multiplexer #(.width(32)) multiplexer_3 (.in0(lo), .in1(negator_3_out), .out(out_lo), .sel(neg));  // open: en
  Negator #(.width(32)) negator_3 (.in(lo), .out(negator_3_out));
  Multiplexer #(.width(32)) multiplexer_4 (.in0(hi), .in1(negator_4_out), .out(out_hi), .sel(neg));  // open: en
  Negator #(.width(32)) negator_4 (.in(hi), .out(negator_4_out));
  // Probe on out_lo
  // Probe on out_hi

  // Other names for the same wires on the sheet: a[31:0] = in_1; _1er_bit_de_a = in_1[31]; b[31:0] = in_3;
  //   _1er_bit_de_b = in_3[31]; result_hi[31:0] = out_hi; result_lo[31:0] = out_lo; sin_signo = in_2
endmodule

module slt_sltu (
  input  [31:0] in_1,
  input  in_2,
  input  [31:0] in_3,
  output [31:0] out
);

  wire comparator_1_lt, comparator_2_lt;
  wire [31:0] b, result_sig, result_unsig;

  // Probe on in_1
  // Probe on in_3
  Comparator #(.width(32)) comparator_1 (.a(in_1), .b(b), .lt(comparator_1_lt));  // open: gt, eq
  Comparator #(.width(32), .mode("unsigned")) comparator_2 (.a(in_1), .b(b), .lt(comparator_2_lt));  // open: gt, eq
  Multiplexer #(.width(32)) multiplexer_1 (
    .in0({32{1'b0}}), .in1(32'h1), .out(result_sig), .sel(comparator_1_lt));  // open: en
  Multiplexer #(.width(32)) multiplexer_2 (
    .in0({32{1'b0}}), .in1(32'h1), .out(result_unsig), .sel(comparator_2_lt));  // open: en
  Multiplexer #(.width(32)) multiplexer_3 (.in0(result_sig), .in1(result_unsig), .out(out), .sel(in_2));  // open: en

  // Other names for the same wires on the sheet: a[31:0] = in_1; b_t[31:0] = in_3; result[31:0] = out;
  //   sin_signo = in_2
endmodule

module andi_ori_xori (
  input  [1:0] in_1,
  input  [31:0] in_2,
  input  [15:0] in_3,
  output [31:0] out
);

  wire [31:0] andi, ori, xori;

  assign andi = in_2 & {{16{1'b0}}, in_3};  // AND_Gate and_1, 32 bits wide
  assign ori = in_2 | {{16{1'b0}}, in_3};  // OR_Gate or_1, 32 bits wide
  assign xori = in_2 ^ {{16{1'b0}}, in_3};  // XOR_Gate xor_1, 32 bits wide
  Multiplexer #(.select(2), .width(32)) multiplexer_1 (
    .in0(andi), .in1(ori), .in2(xori), .out(out), .sel(in_1));  // open: in3, en

  // Other names for the same wires on the sheet: a[31:0] = in_2; b[15:0] = in_3; constante[15:0] = in_3;
  //   result[31:0] = out; selector[1:0] = in_1
endmodule

module slti_sltiu (
  input  [31:0] in_1,
  input  in_2,
  input  [15:0] in_3,
  output [31:0] out
);

  wire comparator_1_lt, neg_a, neg_b;
  wire [31:0] negator_1_out, negator_2_out, result_a, result_b;

  Negator #(.width(32)) negator_1 (.in(in_1), .out(negator_1_out));
  and and_1 (neg_a, in_1[31], in_2);
  Multiplexer #(.width(32)) multiplexer_1 (.in0(in_1), .in1(negator_1_out), .out(result_a), .sel(neg_a));  // open: en
  and and_2 (neg_b, in_3[15], in_2);
  Multiplexer #(.width(32)) multiplexer_2 (
    .in0({{17{in_3[15]}}, in_3[14:0]}), .in1(negator_2_out), .out(result_b), .sel(neg_b));  // open: en
  Negator #(.width(32)) negator_2 (.in({{17{in_3[15]}}, in_3[14:0]}), .out(negator_2_out));
  Comparator #(.width(32)) comparator_1 (.a(result_a), .b(result_b), .lt(comparator_1_lt));  // open: gt, eq
  Multiplexer #(.width(32)) multiplexer_3 (
    .in0({32{1'b0}}), .in1(32'h1), .out(out), .sel(comparator_1_lt));  // open: en

  // Other names for the same wires on the sheet: a[31:0] = in_1; _1er_bit_de_a = in_1[31];
  //   b[31:0] = {{17{in_3[15]}}, in_3[14:0]}; constante[15:0] = in_3; _1er_bit_de_b = in_3[15]; result[31:0] = out;
  //   sin_signo = in_2
endmodule

module sw (
  input  [31:0] in_1,
  input  [15:0] in_2,
  output [3:0] Mask,
  output [15:0] Direccion,
  output [31:0] \output 
);

  wire [31:0] addi_1_out;

  addi addi_1 (.in_1(in_1), .in_2(in_2), .out(addi_1_out));
  // ToRAM toram_1: pin names not known; wires that end beside it: addi_1_out, Mask, Direccion, \output 
endmodule

module addi (
  input  [31:0] in_1,
  input  [15:0] in_2,
  output [31:0] out
);

  Adder #(.width(32)) adder_1 (.a(in_1), .b({{17{in_2[15]}}, in_2[14:0]}), .out(out));  // open: cin, cout

  // Other names for the same wires on the sheet: a[31:0] = in_1; b[31:0] = {{17{in_2[15]}}, in_2[14:0]};
  //   constante[15:0] = in_2; result[31:0] = out
endmodule

module lw (
  input  [31:0] in_1,
  input  [15:0] in_2,
  output [3:0] Mask,
  output [15:0] Direccion,
  output [31:0] \output 
);

  wire [31:0] addi_1_out;

  addi addi_1 (.in_1(in_1), .in_2(in_2), .out(addi_1_out));
  // ToRAM toram_1: pin names not known; wires that end beside it: addi_1_out, Mask, Direccion, \output 
endmodule

module beq (
  input  [15:0] offset,
  input  [31:0] Rs,
  input  [31:0] Rt,
  output [31:0] \output 
);

  wire tunnel;

  Comparator #(.width(32)) comparator_1 (.a(Rs), .b(Rt), .eq(tunnel));  // open: gt, lt
  Multiplexer #(.width(32)) multiplexer_1 (
    .in0({32{1'b0}}), .in1({{15{offset[15]}}, offset[14:0], 2'b00}), .out(\output ), .sel(tunnel));  // open: en

  // Other names for the same wires on the sheet: result[31:2] = {{15{offset[15]}}, offset[14:0]}
endmodule

module bne (
  input  [15:0] offset,
  input  [31:0] Rs,
  input  [31:0] Rt,
  output [31:0] \output 
);

  wire tunnel;

  Comparator #(.width(32)) comparator_1 (.a(Rs), .b(Rt), .eq(tunnel));  // open: gt, lt
  Multiplexer #(.width(32)) multiplexer_1 (
    .in0({{15{offset[15]}}, offset[14:0], 2'b00}), .in1({32{1'b0}}), .out(\output ), .sel(tunnel));  // open: en

  // Other names for the same wires on the sheet: result[31:2] = {{15{offset[15]}}, offset[14:0]}
endmodule

module blez (
  input  [15:0] offset,
  input  [31:0] Rs,
  output [31:0] \output 
);

  wire tunnel, tunnel_t, tunnel_t_t;

  Comparator #(.width(32)) comparator_1 (.a(Rs), .b({32{1'b0}}), .eq(tunnel_t_t), .lt(tunnel));  // open: gt
  or or_1 (tunnel_t, tunnel_t_t, tunnel);
  Multiplexer #(.width(32)) multiplexer_1 (
    .in0({32{1'b0}}), .in1({{15{offset[15]}}, offset[14:0], 2'b00}), .out(\output ), .sel(tunnel_t));  // open: en

  // Other names for the same wires on the sheet: result[31:2] = {{15{offset[15]}}, offset[14:0]}
endmodule

module bgtz (
  input  [15:0] offset,
  input  [31:0] Rs,
  input  [31:0] Rt,
  output [31:0] \output 
);

  wire tunnel;

  Comparator #(.width(32)) comparator_1 (.a(Rs), .b(Rt), .gt(tunnel));  // open: eq, lt
  Multiplexer #(.width(32)) multiplexer_1 (
    .in0({32{1'b0}}), .in1({{15{offset[15]}}, offset[14:0], 2'b00}), .out(\output ), .sel(tunnel));  // open: en

  // Other names for the same wires on the sheet: result[31:2] = {{15{offset[15]}}, offset[14:0]}
endmodule

module bltz (
  input  [15:0] offset,
  input  [31:0] Rs,
  output [31:0] \output 
);

  wire tunnel;

  Comparator #(.width(32)) comparator_1 (.a(Rs), .b({32{1'b0}}), .lt(tunnel));  // open: gt, eq
  Multiplexer #(.width(32)) multiplexer_1 (
    .in0({32{1'b0}}), .in1({{15{offset[15]}}, offset[14:0], 2'b00}), .out(\output ), .sel(tunnel));  // open: en

  // Other names for the same wires on the sheet: result[31:2] = {{15{offset[15]}}, offset[14:0]}
endmodule

module j (
  input  [25:0] Destino,
  input  [31:0] PC,
  output [31:0] Output
);


  assign Output = {PC[31:28], Destino, 2'b00};
endmodule

module kbd (
  input  [6:0] char,
  output [31:0] out
);


  assign out = {{25{1'b0}}, char};
endmodule

module ToRAM (
  input  [31:0] in_1,
  output [1:0] Mask2b,
  output [3:0] Mask,
  output [15:0] Direccion
);

  Decoder #(.select(2)) decoder_1 (
    .out0(Mask[0]), .out1(Mask[1]), .out2(Mask[2]), .out3(Mask[3]), .sel(in_1[3:2]));  // open: en

  assign Direccion = in_1[19:4];
  assign Mask2b = in_1[3:2];

  // Other names for the same wires on the sheet: input[31:0] = in_1; dir[15:0] = in_1[19:4]
endmodule

module Data_Path (
  input  [31:0] in_1,
  input  [6:0] kbd,
  input  Enable_PC,
  input  in_4,
  input  in_5,
  input  in_6,
  input  Enable_SP,
  input  [31:0] in_8,
  output [15:0] Dir_RAM,
  output [15:0] Dir,
  output [3:0] Mask_RAM,
  output [3:0] Mask,
  output [1:0] Mask2b_RAM,
  output [1:0] Mask2b,
  output [31:0] out_15,
  output [6:0] tty_data,
  output [2:0] op_cu,
  output tty,
  output kbd_2,
  output push,
  output lw,
  output [2:0] Sesp
);

  wire alu, en_pila, j, jr, mul_div, rnd, Sbc, sel_p_r_RF, tipo_i;
  wire [1:0] sel_HL, sel_in_RF;
  wire [2:0] bc_t;
  wire [4:0] multiplexer_3_out, Rd, RS, Rt, Salu;
  wire [5:0] Func_code, Op_code;
  wire [15:0] cte;
  wire [25:0] destino;
  wire [31:0] adder_1_out, alu_hi, B, BC, hi, KBD_DATA, lo, multiplexer_1_out, multiplexer_2_out,
       multiplexer_4_out, out_ALU, PC, Ram_Out, SP, undriven;
  wire [31:7] A;

  BC bc_1 (
    .PC(PC), .jmp(j), .FC(Sbc), .in_6(cte), .in_4(destino), .in_5(bc_t), .RS({A, tty_data}), .RT(B),
    .\output (BC));
  kbd kbd_1 (.char(kbd), .out(KBD_DATA));
  Multiplexer #(.width(32)) multiplexer_1 (
    .in0(BC), .in1({A, tty_data}), .out(multiplexer_1_out), .sel(jr));  // open: en
  Adder #(.width(32)) adder_1 (
    .a({A, tty_data}), .b({{17{cte[15]}}, cte[14:0]}), .out(adder_1_out));  // open: cin, cout
  PC pc_1 (
    .out(PC), .Input(multiplexer_1_out), .reset(in_5), .clk(in_6), .enable(Enable_PC), .mask(Mask),
    .address(Dir), .mask_2b(Mask2b));
  Multiplexer #(.width(32)) multiplexer_2 (
    .in0(adder_1_out), .in1(SP), .out(multiplexer_2_out), .sel(en_pila));  // open: en
  ToRAM toram_1 (.in_1(multiplexer_2_out), .Mask(Mask_RAM), .Direccion(Dir_RAM), .Mask2b(Mask2b_RAM));
  ID id_1 (
    .Input(in_1), .Op_Code(Op_code), .Rs(RS), .Rt(Rt), .Rd(Rd), .Func_code(Func_code), .constante(cte),
    .Destino(destino));
  ALU alu_1 (.in_1({A, tty_data}), .in_2(B), .in_3(cte), .in_4(Salu), .Output(out_ALU), .enable(alu), .hi(alu_hi));
  // Probe on sel_in_RF
  Multiplexer #(.width(5)) multiplexer_3 (.in0(Rd), .in1(Rt), .out(multiplexer_3_out), .sel(tipo_i));  // open: en
  // Probe on multiplexer_4_out
  Multiplexer #(.select(2), .width(32)) multiplexer_4 (
    .in0(out_ALU), .in1(undriven), .in2(Ram_Out), .in3(KBD_DATA), .out(multiplexer_4_out), .sel(sel_in_RF));  // open: en
  Priority_Encoder #(.select(2)) priority_encoder_1 (
    .in0(alu), .in1(rnd), .in2(sel_p_r_RF), .in3(kbd_2), .out(sel_in_RF));  // open: gs, en_out, en_in
  or or_1 (sel_p_r_RF, push, lw);
  Selector_Operacion selector_operacion_1 (
    .in_1(Func_code), .in_2(Op_code), .out_7(Salu), .out_4(bc_t), .BC(Sbc), .ALU(alu), .j(j), .out_9(sel_HL),
    .i(tipo_i), .lw(lw), .push(push), .out_11(Sesp), .tipo_op_CU(op_cu), .op_con_div_mul(mul_div),
    .pila(en_pila), .rnd(rnd), .jr(jr), .kbd(kbd_2), .tty(tty));
  RF rf_1 (
    .Selector(multiplexer_3_out), .Input(multiplexer_4_out), .RW(in_4), .Output_A({A, tty_data}),
    .Output_B(B), .Selector_A(RS), .Selector_B(Rt), .Reset(in_5), .clock(in_6), .Output_hi(hi),
    .Output_lo(lo), .in_4(sel_HL), .lo(out_ALU), .hi(alu_hi), .mul_div(mul_div), .in_9(en_pila),
    .in_10(push), .Output_SP(SP), .e_sp(Enable_SP));
  Multiplexer #(.width(32)) multiplexer_5 (.in0(B), .in1({A, tty_data}), .out(out_15), .sel(push));  // open: en
  // Probe on out_15

  // Other names for the same wires on the sheet: A[6:0] = tty_data; adr[15:0] = Dir; bPila = push; bRam = lw;
  //   clk = in_6; Instruccion[31:0] = in_1; kbd_t = kbd_2; ram_input[31:0] = out_15; ram_out_t[31:0] = in_8;
  //   rset = in_5; rw = in_4
endmodule

module BC (
  input  [31:0] PC,
  input  jmp,
  input  FC,
  input  [25:0] in_4,
  input  [2:0] in_5,
  input  [15:0] in_6,
  input  [31:0] RS,
  input  [31:0] RT,
  output [31:0] \output 
);

  wire none;
  wire [1:0] select_op;
  wire [31:0] adder_1_out, beq, bgtz, blez, bltz, bne, Destino_j, DestinoB, j, multiplexer_1_out;

  and and_1 (none, ~jmp, ~FC);  // AND_Gate
  beq beq_1 (.offset(in_6), .Rs(RS), .Rt(RT), .\output (beq));
  bne bne_1 (.offset(in_6), .Rs(RS), .Rt(RT), .\output (bne));
  blez blez_1 (.offset(in_6), .Rs(RS), .\output (blez));
  bgtz bgtz_1 (.offset(in_6), .Rs(RS), .Rt(RT), .\output (bgtz));
  bltz bltz_1 (.offset(in_6), .Rs(RS), .\output (bltz));
  j j_1 (.Destino(in_4), .PC(PC), .Output(j));
  Priority_Encoder #(.select(2)) priority_encoder_1 (
    .in0(jmp), .in1(FC), .in2(none), .out(select_op));  // open: in3, gs, en_out, en_in
  Adder #(.width(32)) adder_1 (.a(PC), .b(32'h4), .out(adder_1_out));  // open: cin, cout
  Multiplexer #(.select(2), .width(32)) multiplexer_1 (
    .in0(Destino_j), .in1(DestinoB), .in2({32{1'b0}}), .out(multiplexer_1_out), .sel(select_op));  // open: in3, en
  // Probe on \output 
  Adder #(.width(32)) adder_2 (.a(adder_1_out), .b(multiplexer_1_out), .out(\output ));  // open: cin, cout
  Multiplexer #(.select(3), .width(32)) multiplexer_2 (
    .in1(beq), .in2(bne), .in3(blez), .in4(bgtz), .in5(bltz), .out(DestinoB), .sel(in_5));  // open: in0, in6, in7, en

  // Other names for the same wires on the sheet: Destino[25:0] = in_4; offset[15:0] = in_6; selector[2:0] = in_5
endmodule

module Selector_Operacion (
  input  [5:0] in_1,
  input  [5:0] in_2,
  output BC,
  output [2:0] out_4,
  output j,
  output i,
  output [4:0] out_7,
  output ALU,
  output [1:0] out_9,
  output jr,
  output [2:0] out_11,
  output op_con_div_mul,
  output tty,
  output kbd,
  output lw,
  output push,
  output pila,
  output rnd,
  output [2:0] tipo_op_CU
);

  wire _0_ALU, _0_BC, _0_opCU, add, addi, alu_i_hilo, \and , and_38_out, and_39_out, andi, beq, bgtz, blez,
       bltz, bne, comparator_5_gt, comparator_5_lt, comparator_6_gt, comparator_6_lt, comparator_7_gt,
       comparator_7_lt, div, divu, esp, halt, hl, j_nada, j_t, mfhi, mflo, mul, mulu, nop, \nor , \or , ori,
       pop, ram, slt, slti, sltiu, sltu, sub, sw, Tipo_E, Tipo_R, Tipo_R1, Tipo_R2, \xor , xori;
  wire [2:0] Operador_E;

  // Probe on in_1
  and and_1 (nop, ~in_1[5], ~in_1[4], ~in_1[3], Tipo_R, ~in_1[2], ~in_1[1], ~in_1[0]);  // AND_Gate
  and and_2 (mulu, ~in_1[5], in_1[4], in_1[3], Tipo_R, ~in_1[2], ~in_1[1], in_1[0]);  // AND_Gate
  and and_3 (sltu, in_1[5], ~in_1[4], in_1[3], Tipo_R, ~in_1[2], in_1[1], in_1[0]);  // AND_Gate
  and and_4 (\xor , in_1[5], ~in_1[4], in_1[3], Tipo_R, ~in_1[2], ~in_1[1], ~in_1[0]);  // AND_Gate
  and and_5 (addi, ~in_2[5], ~in_2[4], in_2[3], i, ~in_2[2], ~in_2[1], ~in_2[0]);  // AND_Gate
  and and_6 (ori, ~in_2[5], ~in_2[4], in_2[3], i, in_2[2], ~in_2[1], in_2[0]);  // AND_Gate
  and and_7 (pop, ~in_1[5], ~in_1[4], ~in_1[3], Tipo_R2, ~in_1[2], ~in_1[1], ~in_1[0]);  // AND_Gate
  and and_8 (blez, ~in_2[5], ~in_2[4], ~in_2[3], i, in_2[2], in_2[1], ~in_2[0]);  // AND_Gate
  and and_9 (halt, in_1[5], in_1[4], in_1[3], Tipo_E, in_1[2], in_1[1], in_1[0]);
  and and_10 (j_t, ~in_1[5], ~in_1[4], ~in_1[3], j, ~in_1[2], in_1[1], ~in_1[0]);  // AND_Gate
  Comparator #(.width(6)) comparator_1 (.a(in_2), .b({6{1'b0}}), .eq(Tipo_R));  // open: gt, lt
  Comparator #(.width(6)) comparator_2 (.a(in_2), .b({6{1'b1}}), .eq(Tipo_E));  // open: gt, lt
  Comparator #(.width(6)) comparator_3 (.a(in_2), .b(6'b000010), .eq(j));  // open: gt, lt
  and and_11 (i, ~Tipo_R1, ~Tipo_E, ~j);  // AND_Gate
  and and_12 (add, in_1[5], ~in_1[4], ~in_1[3], Tipo_R, ~in_1[2], ~in_1[1], ~in_1[0]);  // AND_Gate
  and and_13 (div, ~in_1[5], in_1[4], in_1[3], Tipo_R, ~in_1[2], in_1[1], ~in_1[0]);  // AND_Gate
  and and_14 (\and , in_1[5], ~in_1[4], ~in_1[3], Tipo_R, in_1[2], ~in_1[1], ~in_1[0]);  // AND_Gate
  and and_15 (jr, ~in_1[5], ~in_1[4], in_1[3], Tipo_R, ~in_1[2], ~in_1[1], ~in_1[0]);  // AND_Gate
  and and_16 (slti, ~in_2[5], ~in_2[4], in_2[3], i, ~in_2[2], in_2[1], ~in_2[0]);  // AND_Gate
  and and_17 (xori, ~in_2[5], ~in_2[4], in_2[3], i, in_2[2], in_2[1], ~in_2[0]);  // AND_Gate
  and and_18 (push, ~in_1[5], ~in_1[4], ~in_1[3], Tipo_R2, ~in_1[2], ~in_1[1], in_1[0]);  // AND_Gate
  and and_19 (bgtz, ~in_2[5], ~in_2[4], ~in_2[3], i, in_2[2], in_2[1], in_2[0]);  // AND_Gate
  and and_20 (tty, ~in_1[5], ~in_1[4], ~in_1[3], Tipo_E, ~in_1[2], ~in_1[1], in_1[0]);  // AND_Gate
  or or_1 (Tipo_R1, Tipo_R, Tipo_R2);
  Comparator #(.width(6)) comparator_4 (.a(in_2), .b(6'b111000), .eq(Tipo_R2));  // open: gt, lt
  // Probe on 2'b00
  Comparator #(.width(3)) comparator_5 (.a(out_4), .b(3'b000), .gt(comparator_5_gt), .lt(comparator_5_lt));  // open: eq
  or or_2 (ALU, comparator_6_gt, comparator_6_lt);
  Comparator #(.width(5)) comparator_6 (
    .a(out_7), .b({5{1'b0}}), .gt(comparator_6_gt), .lt(comparator_6_lt));  // open: eq
  or or_3 (hl, comparator_7_gt, comparator_7_lt);
  Comparator #(.width(2)) comparator_7 (.a(out_9), .b(2'b00), .gt(comparator_7_gt), .lt(comparator_7_lt));  // open: eq
  and and_21 (sub, in_1[5], ~in_1[4], ~in_1[3], Tipo_R, ~in_1[2], in_1[1], ~in_1[0]);  // AND_Gate
  and and_22 (divu, ~in_1[5], in_1[4], in_1[3], Tipo_R, ~in_1[2], in_1[1], in_1[0]);  // AND_Gate
  and and_23 (\or , in_1[5], ~in_1[4], ~in_1[3], Tipo_R, in_1[2], ~in_1[1], in_1[0]);  // AND_Gate
  and and_24 (mfhi, ~in_1[5], in_1[4], ~in_1[3], Tipo_R, ~in_1[2], ~in_1[1], ~in_1[0]);  // AND_Gate
  and and_25 (sltiu, ~in_2[5], ~in_2[4], in_2[3], i, ~in_2[2], in_2[1], in_2[0]);  // AND_Gate
  and and_26 (lw, in_2[5], ~in_2[4], ~in_2[3], i, ~in_2[2], in_2[1], in_2[0]);  // AND_Gate
  and and_27 (beq, ~in_2[5], ~in_2[4], ~in_2[3], i, in_2[2], ~in_2[1], ~in_2[0]);  // AND_Gate
  and and_28 (bltz, ~in_2[5], ~in_2[4], ~in_2[3], i, ~in_2[2], ~in_2[1], in_2[0]);  // AND_Gate
  and and_29 (rnd, ~in_1[5], ~in_1[4], ~in_1[3], Tipo_E, ~in_1[2], in_1[1], ~in_1[0]);  // AND_Gate
  or or_4 (BC, comparator_5_gt, comparator_5_lt);
  and and_30 (mul, ~in_1[5], in_1[4], in_1[3], Tipo_R, ~in_1[2], ~in_1[1], ~in_1[0]);  // AND_Gate
  and and_31 (slt, in_1[5], ~in_1[4], in_1[3], Tipo_R, ~in_1[2], in_1[1], ~in_1[0]);  // AND_Gate
  and and_32 (\nor , in_1[5], ~in_1[4], ~in_1[3], Tipo_R, in_1[2], in_1[1], in_1[0]);  // AND_Gate
  and and_33 (mflo, ~in_1[5], in_1[4], ~in_1[3], Tipo_R, ~in_1[2], in_1[1], ~in_1[0]);  // AND_Gate
  and and_34 (andi, ~in_2[5], ~in_2[4], in_2[3], i, in_2[2], ~in_2[1], ~in_2[0]);  // AND_Gate
  and and_35 (sw, in_2[5], ~in_2[4], in_2[3], i, ~in_2[2], in_2[1], in_2[0]);  // AND_Gate
  and and_36 (bne, ~in_2[5], ~in_2[4], ~in_2[3], i, in_2[2], ~in_2[1], in_2[0]);  // AND_Gate
  and and_37 (kbd, ~in_1[5], ~in_1[4], ~in_1[3], Tipo_E, in_1[2], ~in_1[1], ~in_1[0]);  // AND_Gate
  or or_5 (alu_i_hilo, BC, ALU, hl);
  or or_6 (j_nada, j, nop);
  or or_7 (ram, lw, sw);
  or or_8 (pila, pop, push);
  Comparator #(.width(3)) comparator_8 (.a(Operador_E), .b(3'b000), .gt(esp));  // open: eq, lt
  and and_38 (and_38_out, ~mfhi, ~mflo);  // AND_Gate
  // Probe on out_4
  Priority_Encoder priority_encoder_1 (
    .in0(_0_BC), .in1(beq), .in2(bne), .in3(blez), .in4(bgtz), .in5(bltz), .out(out_4));  // open: in6, in7, en_in, gs, en_out
  Priority_Encoder #(.select(2)) priority_encoder_2 (
    .in0(and_38_out), .in1(mfhi), .in2(mflo), .out(out_9));  // open: in3, gs, en_out, en_in
  // Probe on out_9
  and and_39 (and_39_out, ~halt, ~tty, ~rnd, ~kbd);  // AND_Gate
  or or_9 (op_con_div_mul, mul, mulu, div, divu);
  Priority_Encoder #(.select(5)) priority_encoder_3 (
    .in0(_0_ALU), .in1(add), .in2(sub), .in3(mul), .in4(mulu), .in5(div), .in6(divu), .in7(slt), .in8(sltu),
    .in9(\and ), .in10(\or ), .in11(\nor ), .in12(\xor ), .in13(addi), .in14(slti), .in15(sltiu),
    .in16(andi), .in17(ori), .in18(xori), .out(out_7));  // open: in19, in20, in21, in22, in23, in24, in25, in26, in27, in28, in29, in30, in31, gs, en_out, en_in
  Priority_Encoder #(.disabled(0)) priority_encoder_4 (
    .in0(and_39_out), .in1(halt), .in2(tty), .in3(rnd), .in4(kbd), .out(out_11));  // open: in5, in6, in7, en_in, gs, en_out
  Priority_Encoder #(.disabled(0)) priority_encoder_5 (
    .in0(_0_opCU), .in1(alu_i_hilo), .in2(j_nada), .in3(ram), .in4(pila), .in5(esp), .out(tipo_op_CU));  // open: in6, in7, en_in, gs, en_out
  // Probe on out_7
  and and_40 (_0_opCU, ~alu_i_hilo, ~j_nada, ~ram, ~pila, ~esp);  // AND_Gate
  and and_41 (_0_BC, ~beq, ~bne, ~blez, ~bgtz, ~bltz);  // AND_Gate
  and and_42 (_0_ALU, ~add, ~sub, ~mul, ~mulu, ~div, ~divu, ~slt, ~sltu, ~\and , ~\nor , ~\xor , ~addi, ~slti, ~sltiu, ~andi, ~ori, ~xori, ~\or );  // AND_Gate

  // Other names for the same wires on the sheet: F5 = in_1[0]; Func_Code[5:0] = in_1; F4 = in_1[1]; F3 = in_1[2];
  //   F2 = in_1[3]; F1 = in_1[4]; F0 = in_1[5]; O5 = in_2[0]; Op_Code[5:0] = in_2; O4 = in_2[1]; O3 = in_2[2];
  //   O2 = in_2[3]; O1 = in_2[4]; O0 = in_2[5]; Operador_ALU[4:0] = out_7; Operador_BC[2:0] = out_4;
  //   Operador_E_t[2:0] = out_11; Operador_HL[1:0] = out_9; Tipo_I = i; Tipo_J = j

  // Notes on the sheet:
  //   TIPO R
  //   TIPO I
  //   TIPO Especial
  //   TIPO J
endmodule

module PC (
  input  [31:0] Input,
  input  enable,
  input  clk,
  input  reset,
  output [31:0] out,
  output [3:0] mask,
  output [15:0] address,
  output [1:0] mask_2b
);

  Register #(.width(32)) register_1 (.D(Input), .en(enable), .Q(out), .clk(clk), .clr(reset));
  // Probe on out
  ToRAM toram_1 (.in_1(out), .Mask(mask), .Direccion(address), .Mask2b(mask_2b));
endmodule

module CU (
  input  in_1,
  input  [2:0] in_2,
  input  in_3,
  input  [3:0] in_4,
  input  [2:0] in_5,
  input  [3:0] in_6,
  input  in_7,
  input  in_8,
  output RF_WR,
  output tty,
  output e_SP,
  output kbd,
  output halt,
  output enable_PC,
  output en_ram_p_lw,
  output CS,
  output leer_ram,
  output en_ram_ins
);

  wire ALU_I1, ALU_I2, and_1_out, and_2_out, aux, CS1, CS3, CS4, CS5, CS6, d_ff_2_q, d_ff_4_q, d_ff_5_q,
       d_ff_7_q, d_ff_8_q, d_ff_15_q, d_ff_16_q, d_ff_19_q, demultiplexer_1_out0, demultiplexer_3_out0,
       demultiplexer_4_out5, demultiplexer_5_out0, demultiplexer_5_out1, demultiplexer_7_out0,
       demultiplexer_7_out1, demultiplexer_8_out0, demultiplexer_8_out1, demultiplexer_9_out0, e_SP0, e_SP1,
       en_ram_ins0, en_ram_ins1, en_ram_ins2, en_ram_p_lw_0, en_ram_p_lw_1, fin_escribir_leer, halt1,
       jump_nada, kbd1, kbd2, nor_1_out, or_2_out, or_4_out, or_5_out, or_6_out, or_7_out, or_9_out,
       or_13_out, pila1, pila2, ram1, ram2, RF_WR2, RF_WR6, RF_WR7, rnd2, start, xnor_1_out;
  wire [3:0] counter_1_q, Tiempo_espera;

  and and_1 (and_1_out, ~in_2[2], in_2[1], ~in_2[0], in_7);  // AND_Gate
  Demultiplexer demultiplexer_1 (.out0(demultiplexer_1_out0), .out1(e_SP0), .in(pila1), .sel(in_8));  // open: en
  or or_1 (en_ram_ins0, en_ram_ins2, start);
  Multiplexer #(.width(4)) multiplexer_1 (.in0(in_4), .in1(in_6), .out(Tiempo_espera), .sel(or_2_out));  // open: en
  or or_2 (or_2_out, and_1_out, and_2_out);
  and and_2 (and_2_out, in_8, ~in_2[2], in_2[1], in_2[0]);  // AND_Gate
  D_Flip_Flop #(.trigger("falling")) d_ff_1 (.clk(in_3), .D(ALU_I1), .Q(ALU_I2), .reset(in_1));  // open: Qn, preset, en
  D_Flip_Flop #(.trigger("falling")) d_ff_2 (
    .clk(in_3), .D(demultiplexer_1_out0), .Q(d_ff_2_q), .reset(in_1));  // open: Qn, preset, en
  or or_3 (halt, d_ff_4_q, halt1);
  Demultiplexer demultiplexer_2 (
    .out0(en_ram_ins2), .out1(en_ram_ins1), .in(CS6), .sel(fin_escribir_leer));  // open: en
  D_Flip_Flop #(.trigger("falling")) d_ff_3 (
    .clk(in_3), .D(en_ram_ins0), .Q(CS6), .preset(in_1));  // open: Qn, en, reset
  or or_4 (or_4_out, demultiplexer_3_out0, d_ff_2_q);
  D_Flip_Flop #(.trigger("falling")) d_ff_4 (.clk(in_3), .D(halt), .Q(d_ff_4_q), .reset(in_1));  // open: Qn, preset, en
  xnor xnor_1 (xnor_1_out, aux, nor_1_out);
  D_Flip_Flop #(.trigger("falling")) d_ff_5 (.clk(in_3), .D(ram1), .Q(d_ff_5_q), .reset(in_1));  // open: Qn, preset, en
  D_Flip_Flop #(.trigger("falling")) d_ff_6 (.clk(in_3), .D(or_4_out), .Q(CS4), .reset(in_1));  // open: Qn, preset, en
  Demultiplexer demultiplexer_3 (
    .out0(demultiplexer_3_out0), .out1(en_ram_p_lw_0), .in(CS4), .sel(fin_escribir_leer));  // open: en
  D_Flip_Flop #(.trigger("falling")) d_ff_7 (
    .clk(in_3), .D(e_SP0), .Q(d_ff_7_q), .reset(in_1));  // open: Qn, preset, en
  D_Flip_Flop #(.trigger("falling")) d_ff_8 (
    .clk(in_3), .D(en_ram_ins1), .Q(d_ff_8_q), .reset(in_1));  // open: Qn, preset, en
  Demultiplexer #(.select(3)) demultiplexer_4 (
    .out1(ALU_I1), .out2(jump_nada), .out3(ram1), .out4(pila1), .out5(demultiplexer_4_out5), .in(d_ff_8_q),
    .sel(in_2));  // open: out0, out6, out7, en
  // Probe on in_2
  or or_5 (or_5_out, ~xnor_1_out, CS);  // OR_Gate
  Demultiplexer demultiplexer_5 (
    .out0(demultiplexer_5_out0), .out1(demultiplexer_5_out1), .in(d_ff_5_q), .sel(in_7));  // open: en
  D_Flip_Flop #(.trigger("falling")) d_ff_9 (.clk(in_3), .D(or_5_out), .Q(aux), .reset(in_1));  // open: Qn, preset, en
  D_Flip_Flop #(.trigger("falling")) d_ff_10 (.clk(in_3), .D(or_6_out), .Q(CS1), .reset(in_1));  // open: Qn, preset, en
  or or_6 (or_6_out, demultiplexer_7_out0, demultiplexer_5_out0);
  or or_7 (or_7_out, demultiplexer_8_out0, d_ff_7_q);
  or or_8 (en_ram_p_lw, en_ram_p_lw_0, en_ram_p_lw_1);
  Demultiplexer #(.select(3)) demultiplexer_6 (
    .out1(halt1), .out2(RF_WR6), .out3(RF_WR7), .out4(kbd1), .in(demultiplexer_4_out5), .sel(in_5));  // open: out0, out5, out6, out7, en
  Counter #(.width(4), .max('hf)) counter_1 (
    .load(or_5_out), .D(Tiempo_espera), .count(aux), .Q(counter_1_q), .clk(in_3), .clr(in_1));  // open: carry
  Demultiplexer demultiplexer_7 (
    .out0(demultiplexer_7_out0), .out1(demultiplexer_7_out1), .in(CS1), .sel(fin_escribir_leer));  // open: en
  D_Flip_Flop #(.trigger("falling")) d_ff_11 (.clk(in_3), .D(or_7_out), .Q(CS5), .reset(in_1));  // open: Qn, preset, en
  Demultiplexer demultiplexer_8 (
    .out0(demultiplexer_8_out0), .out1(demultiplexer_8_out1), .in(CS5), .sel(fin_escribir_leer));  // open: en
  D_Flip_Flop #(.trigger("falling")) d_ff_12 (.clk(in_3), .D(RF_WR6), .Q(tty), .reset(in_1));  // open: Qn, preset, en
  nor nor_1 (nor_1_out, counter_1_q[0], counter_1_q[1], counter_1_q[2], counter_1_q[3]);
  or or_9 (or_9_out, demultiplexer_9_out0, demultiplexer_5_out1);
  D_Flip_Flop #(.trigger("falling")) d_ff_13 (
    .clk(in_3), .D(en_ram_p_lw_0), .Q(e_SP1), .reset(in_1));  // open: Qn, preset, en
  and and_3 (fin_escribir_leer, nor_1_out, aux);
  D_Flip_Flop #(.trigger("falling")) d_ff_14 (.clk(in_3), .D(or_9_out), .Q(CS3), .reset(in_1));  // open: Qn, preset, en
  D_Flip_Flop #(.trigger("falling")) d_ff_15 (
    .clk(in_3), .D(e_SP1), .Q(d_ff_15_q), .reset(in_1));  // open: Qn, preset, en
  D_Flip_Flop #(.trigger("falling")) d_ff_16 (
    .clk(in_3), .D(demultiplexer_8_out1), .Q(d_ff_16_q), .reset(in_1));  // open: Qn, preset, en
  or or_10 (CS, CS1, CS3, CS4, CS5, CS6);
  or or_11 (leer_ram, CS3, CS4, CS6);
  Demultiplexer demultiplexer_9 (
    .out0(demultiplexer_9_out0), .out1(en_ram_p_lw_1), .in(CS3), .sel(fin_escribir_leer));  // open: en
  or or_12 (pila2, d_ff_15_q, d_ff_16_q);
  or or_13 (or_13_out, tty, rnd2, kbd2);
  D_Flip_Flop #(.trigger("falling")) d_ff_17 (
    .clk(in_3), .D(en_ram_p_lw_1), .Q(RF_WR2), .reset(in_1));  // open: Qn, preset, en
  D_Flip_Flop #(.trigger("falling")) d_ff_18 (.clk(in_3), .D(RF_WR7), .Q(rnd2), .reset(in_1));  // open: Qn, preset, en
  or or_14 (enable_PC, ALU_I2, jump_nada, ram2, pila2, or_13_out);
  D_Flip_Flop #(.trigger("falling")) d_ff_19 (
    .clk(in_3), .D(RF_WR2), .Q(d_ff_19_q), .reset(in_1));  // open: Qn, preset, en
  or or_15 (RF_WR, ALU_I1, RF_WR2, e_SP1, RF_WR6, RF_WR7, kbd);
  or or_16 (ram2, demultiplexer_7_out1, d_ff_19_q);
  D_Flip_Flop #(.trigger("falling")) d_ff_20 (.clk(in_3), .D(kbd1), .Q(kbd), .reset(in_1));  // open: Qn, preset, en
  or or_17 (en_ram_ins, en_ram_ins0, en_ram_ins2, CS6, en_ram_ins1);
  D_Flip_Flop #(.trigger("falling")) d_ff_21 (
    .clk(in_3), .D(enable_PC), .Q(start), .reset(in_1));  // open: Qn, preset, en
  D_Flip_Flop #(.trigger("falling")) d_ff_22 (.clk(in_3), .D(kbd), .Q(kbd2), .reset(in_1));  // open: Qn, preset, en
  or or_18 (e_SP, e_SP0, e_SP1);

  // Other names for the same wires on the sheet: clk = in_3; RF_WR3 = e_SP1; Enable_Pc1 = enable_PC; escribir1 = CS1;
  //   escribir2 = CS5; leer2 = CS3; leer4 = CS4; en_ram_ins3 = CS6; leer6 = CS6; lw = in_7; Operador_E[2:0] = in_5;
  //   out_halt = halt; out_kbd = kbd; RF_WR8 = kbd; push = in_8; reset = in_1; RF_WR1 = ALU_I1; rnd1 = RF_WR7;
  //   Tiempo_escribir[3:0] = in_6; Tiempo_leer[3:0] = in_4; tipo_operacion[2:0] = in_2; tty1 = RF_WR6; out_tty = tty;
  //   tty2 = tty

  // Notes on the sheet:
  //   ALU/I/MF
  //   Push/Pop
  //   HALT
  //   Tiempo de espera
  //   LW/SW
  //   TTY
  //   RND
  //   KBD
endmodule

module Ciclo (
  input  clk,
  input  \input ,
  input  \final ,
  input  reset,
  output out_5
);

  wire d_ff_1_q, demultiplexer_1_out0;

  // OR_Gate or_1 has open pins: in0=demultiplexer_1_out0, in1=\input , out=open
  D_Flip_Flop #(.trigger("falling")) d_ff_1 (.clk(clk), .Q(d_ff_1_q), .preset(reset));  // open: D, Qn, en, reset
  Demultiplexer demultiplexer_1 (.out0(demultiplexer_1_out0), .out1(out_5), .in(d_ff_1_q), .en(\final ));  // open: sel
endmodule

module inv (
  input  [31:0] in_1,
  output [31:0] out_2
);


  assign out_2 = {in_1[7:0], in_1[15:8], in_1[23:16], in_1[31:24]};
endmodule
